# Fritzing sketch car (saved by Fritzing 0.9.4)

parts:
  Компонент1 = Arduino Nano (Rev3.0)
  Raspberry_Pi_1 = Raspberry Pi 3 [part_number=RPI-3-V1.2]
  Компонент2 = Voltage Sensor 25V
  M1 = ESC
  920KV_Motor2 = DJI 920 KV Motor
  J1 = Basic Servo
  Компонент3 = Voltage Sensor 25V
  U1 = LIPO-2000mAh [package=lipo-2000]
  U2 = LIPO-1000mAh [package=lipo-1000]  # not connected
  Conn_9 = USB connector [package=THT]
  Компонент4 = DC-DC Power Module (5v)

nets:
  GND: Компонент1.GND, Raspberry_Pi_1.GND, Компонент2.-, M1.GND, J1.gnd, Компонент3.-
  VIN: Компонент1.VIN, Raspberry_Pi_1.5V
  VCC: Компонент1.5V, Компонент2.VCC, Компонент2.+, Компонент3.VCC, Компонент3.+, U1.+, Компонент4.Vin
  N1: Компонент1.A5, Raspberry_Pi_1.GPIO3
  N2: Компонент1.A4, Raspberry_Pi_1.GPIO2
  N3: Компонент1.A1, Компонент3.S
  N4: Компонент1.A0, Компонент2.S
  N5: Raspberry_Pi_1.GPIO13, M1.DATA
  N6: Raspberry_Pi_1.GPIO12, J1.pulse
  N7: M1.U, 920KV_Motor2.u
  N8: M1.V, 920KV_Motor2.v
  N9: M1.W, 920KV_Motor2.w
  N10: M1.pin_8, J1.vcc
  GND_2: Компонент3.GND, U1.-, Компонент4.GND
  N11: Conn_9.5V, Компонент4.Vout
  N12: Conn_9.GND, Conn_9.chassis5, Conn_9.chassis6, Компонент4.GND*

notes:
  USB 5V Power
  ESC + Main Motor
  Steering Servo
  Voltage Sensor
  Arduino Nano
  Raspberry Pi 3
  Motor Battery
  RPi Battery

custom parts:
  DJI 920 KV Motor: DJI Brushless Outrunner 2212/920K Motor F330-550
  DC-DC Power Module (5v): DC-DC Power Module based con AMS1117-5.0 Input: DC 6~12V (input power must higher 1V than output power); Output: 5V (+/-0.05V error), 800mA
